# Fritzing sketch battery-toolbox (saved by Fritzing 0.9.6b)
breadboards: 1

parts:
  Part1 = Arduino Uno (Rev3)
  R1 = Trimmer Potentiometer [maximum_resistance=25kΩ package=THT]
  U2 = LCD-16X2 [package=lcd-16x2_nosilk]
  R2 = Resistor [tolerance=±5% power=0.25 resistance=220 package=THT]
  U3 = ENCODER-QUADRATURE [package=encoder-16mm-quad]
  C1 = Ceramic Capacitor [capacitance=100nF voltage=35V package="100 mil [THT, multilayer]"]
  C2 = Ceramic Capacitor [capacitance=100nF voltage=35V package="100 mil [THT, multilayer]"]
  S1_(Rotary_Push) = Pushbutton [package="[THT]"]
  C3 = Ceramic Capacitor [capacitance=100nF voltage=35V package="100 mil [THT, multilayer]"]
  D1 = Zener Diode [breakdown_voltage=4.7V package="Melf DO-213 AB [SMD]"]
  R3 = Resistor [tolerance=±5% power=0.25 resistance=22 package=THT]
  R4 = Resistor [tolerance=±1% power=0.25 resistance=20k package=THT]
  R5 = Trimmer Potentiometer [maximum_resistance=5k package=THT]
  R6 = Resistor [tolerance=±1% power=0.25W resistance=6190 package=THT]
  R7 = Resistor [tolerance=±5% power=0.25 resistance=50k package=THT]
  U4 = ACS712 [package=so08]
  C4 = Ceramic Capacitor [capacitance=1nF voltage=35V package="100 mil [THT, multilayer]"]
  R8 = Resistor [tolerance=±5% power=0.25 resistance=47k package=THT]
  R9 = Resistor [tolerance=±5% power=0.25 resistance=1.8k package=THT]
  C5 = Ceramic Capacitor [capacitance=100nF voltage=35V package="100 mil [THT, multilayer]"]
  V2 = DC Power [voltage=12V part_number="Car Battery"]  # not connected
  Q1 = Basic FET N-Channel [part_number=D472 package="D2Pak [SMD]"]  # not connected

nets:
  N1: Part1.A0, R5.wiper
  N2: Part1.A1, R8.Pin_1, R9.Pin_0, C5.1
  N3: Part1.A4/SDA, S1_(Rotary_Push).Pin_2, C3.1, R7.Pin_0
  N4: Part1.D8, U2.DB4
  N5: Part1.D12/MISO, U2.E
  N6: Part1.D13/SCK, U2.RS
  GND: Part1.GND, R1.leg2, U2.VSS, U2.R_W, U3.C, C1.0, C2.1, S1_(Rotary_Push).Pin_4, C3.0, D1.anode, R6.Pin_1, U4.GND, C4.0
  N7: Part1.AREF, D1.cathode, R3.Pin_0
  N8: Part1.D2, U3.A, C1.1
  N9: Part1.D3_PWM, U3.B, C2.0
  N10: Part1.D4, U2.DB7
  N11: Part1.D5_PWM, U2.DB6
  N12: Part1.D7, U2.DB5
  5V: Part1.5V, R1.leg1, U2.VDD, U2.K, R2.Pin_1, R3.Pin_1, R4.Pin_0, R7.Pin_1, U4.VCC
  5V_2: Part1.VIN
  N13: R1.wiper, U2.VO
  N14: U2.A, R2.Pin_0
  N15: R4.Pin_1, R5.leg1
  N16: R5.leg2, R6.Pin_0
  N17: U4.FILT, C4.1
  N18: U4.VOUT, R9.Pin_1
  N19: R8.Pin_0, C5.0
